// Logisim project B21CS098.circ as structural Verilog: 3 circuits, main circuit main
module main (
  input  [31:0] Binary_Instruction,
  output Jump,
  output ALURequired,
  output RegDest,
  output Branch,
  output MemWrite,
  output MemRead,
  output MemToReg,
  output RegWrite,
  output ALUSrc,
  output [1:0] ALUOp,
  output ADD,
  output SUB,
  output AND,
  output OR,
  output XOR,
  output SLT,
  output Not_R_type
);

  wire control_unit_1_r_type;
  wire [5:0] control_unit_1_funct;

  Control_unit control_unit_1 (
    .Binary_Instruction(Binary_Instruction), .Jump(Jump), .ALURequired(ALURequired), .RegDest(RegDest),
    .Branch(Branch), .MemWrite(MemWrite), .MemRead(MemRead), .MemToReg(MemToReg), .RegWrite(RegWrite),
    .ALUSrc(ALUSrc), .ALUOp(ALUOp), .Funct(control_unit_1_funct), .R_type(control_unit_1_r_type));
  ALU_Op_Exe alu_op_exe_1 (
    .Funct(control_unit_1_funct), .R_type(control_unit_1_r_type), .ADD(ADD), .SUB(SUB), .AND(AND), .OR(OR),
    .XOR(XOR), .SLT(SLT), .Not_R_type(Not_R_type));

  // Notes on the sheet:
  //   R-type
  //   Funct
endmodule

module ALU_Op_Exe (
  input  [5:0] Funct,
  input  R_type,
  output ADD,
  output SUB,
  output AND,
  output OR,
  output XOR,
  output SLT,
  output Not_R_type
);

  wire [3:0] multiplexer_1_out;

  Multiplexer #(.width(4), .enable("false")) multiplexer_1 (
    .in0(4'b0001), .in1(Funct[3:0]), .out(multiplexer_1_out), .sel(R_type));
  and u_ADD (ADD, ~multiplexer_1_out[3], ~multiplexer_1_out[2], ~multiplexer_1_out[1], ~multiplexer_1_out[0]);  // AND_Gate
  and u_SUB (SUB, ~multiplexer_1_out[3], ~multiplexer_1_out[2], multiplexer_1_out[1], ~multiplexer_1_out[0]);  // AND_Gate
  and u_AND (AND, ~multiplexer_1_out[3], multiplexer_1_out[2], ~multiplexer_1_out[1], ~multiplexer_1_out[0]);  // AND_Gate
  and u_XOR (XOR, ~multiplexer_1_out[3], multiplexer_1_out[2], multiplexer_1_out[1], ~multiplexer_1_out[0]);  // AND_Gate
  and u_OR (OR, ~multiplexer_1_out[3], multiplexer_1_out[2], ~multiplexer_1_out[1], multiplexer_1_out[0]);  // AND_Gate
  and u_SLT (SLT, multiplexer_1_out[3], ~multiplexer_1_out[2], multiplexer_1_out[1], ~multiplexer_1_out[0]);  // AND_Gate
  and and_2 (Not_R_type, ~multiplexer_1_out[3], ~multiplexer_1_out[2], ~multiplexer_1_out[1], multiplexer_1_out[0]);  // AND_Gate
endmodule

module Control_unit (
  input  [31:0] Binary_Instruction,
  output [5:0] Funct,
  output Jump,
  output ALURequired,
  output RegDest,
  output Branch,
  output MemWrite,
  output MemRead,
  output MemToReg,
  output RegWrite,
  output ALUSrc,
  output R_type,
  output [1:0] ALUOp
);

  wire ADDI_out, ANDI_out, BEQ_out, BNE_out, ORI_out, SLTI_out, XORI_out;

  and u_R_type (R_type, ~Binary_Instruction[31], ~Binary_Instruction[30], ~Binary_Instruction[29], ~Binary_Instruction[28], ~Binary_Instruction[27], ~Binary_Instruction[26]);  // AND_Gate
  and LW (MemRead, Binary_Instruction[31], ~Binary_Instruction[30], ~Binary_Instruction[29], ~Binary_Instruction[28], Binary_Instruction[27], Binary_Instruction[26]);  // AND_Gate
  and SW (MemWrite, Binary_Instruction[31], ~Binary_Instruction[30], Binary_Instruction[29], ~Binary_Instruction[28], Binary_Instruction[27], Binary_Instruction[26]);  // AND_Gate
  and BEQ (BEQ_out, ~Binary_Instruction[31], ~Binary_Instruction[30], ~Binary_Instruction[29], Binary_Instruction[28], ~Binary_Instruction[27], ~Binary_Instruction[26]);  // AND_Gate
  and ADDI (ADDI_out, ~Binary_Instruction[31], ~Binary_Instruction[30], Binary_Instruction[29], ~Binary_Instruction[28], ~Binary_Instruction[27], ~Binary_Instruction[26]);  // AND_Gate
  and SLTI (SLTI_out, ~Binary_Instruction[31], ~Binary_Instruction[30], Binary_Instruction[29], ~Binary_Instruction[28], Binary_Instruction[27], ~Binary_Instruction[26]);  // AND_Gate
  and ANDI (ANDI_out, ~Binary_Instruction[31], ~Binary_Instruction[30], Binary_Instruction[29], Binary_Instruction[28], ~Binary_Instruction[27], ~Binary_Instruction[26]);  // AND_Gate
  and ORI (ORI_out, ~Binary_Instruction[31], ~Binary_Instruction[30], Binary_Instruction[29], Binary_Instruction[28], ~Binary_Instruction[27], Binary_Instruction[26]);  // AND_Gate
  and XORI (XORI_out, ~Binary_Instruction[31], ~Binary_Instruction[30], Binary_Instruction[29], Binary_Instruction[28], Binary_Instruction[27], ~Binary_Instruction[26]);  // AND_Gate
  ROM #(.addrWidth(6), .dataWidth(2)) rom_1 (.addr(Binary_Instruction[31:26]), .data(ALUOp));  // open: sel
  and J (Jump, ~Binary_Instruction[31], ~Binary_Instruction[30], ~Binary_Instruction[29], ~Binary_Instruction[28], Binary_Instruction[27], ~Binary_Instruction[26]);  // AND_Gate
  and BNE (BNE_out, ~Binary_Instruction[31], ~Binary_Instruction[30], ~Binary_Instruction[29], Binary_Instruction[28], ~Binary_Instruction[27], Binary_Instruction[26]);  // AND_Gate
  not not_1 (ALURequired, Jump);
  or or_1 (Branch, BNE_out, BEQ_out);
  or u_RegWrite (RegWrite, XORI_out, ORI_out, ANDI_out, SLTI_out, ADDI_out, MemRead, R_type);
  nor nor_1 (ALUSrc, BNE_out, BEQ_out, R_type);

  assign Funct = Binary_Instruction[5:0];
  assign MemToReg = MemRead;
  assign RegDest = R_type;

  // Other names for the same wires on the sheet: Opcode[5:0] = Binary_Instruction[31:26]

  // Notes on the sheet:
  //   contents of rom_1 (hex, n*v repeats v):
  //   2 0 0 0 1 1 4*0 3 0 3 3 3
endmodule
