// Logisim project B21CS098.circ as structural Verilog: 4 circuits, main circuit main
module main (
  input  [31:0] _32_Bit__Instruction_Code,
  input  [31:0] Register_RS,
  input  [31:0] Register_RT,
  output RegDst,
  output Overflow_Condition,
  output Branch,
  output MemRead,
  output MemToReg,
  output ALUOpHi,
  output ALUOpLo,
  output UnderFlow_Condition,
  output MemWrite,
  output ALUSrc,
  output RegWrite,
  output Zero,
  output [31:0] _32_bit_ALU_Output,
  output out_17,
  output out_18,
  output out_19,
  output out_20
);

  wire and_2_out, and_3_out, and_4_out, and_5_out, not_1_out, not_2_out, not_3_out, not_4_out;
  wire [31:0] adder_1_out, and_1_out, bit_extender_1_out, multiplexer_1_out, or_1_out, subtractor_1_out;

  control_unit ControlUnit (
    .B31(_32_Bit__Instruction_Code[31]), .B30(_32_Bit__Instruction_Code[30]),
    .B29(_32_Bit__Instruction_Code[29]), .B28(_32_Bit__Instruction_Code[28]),
    .B27(_32_Bit__Instruction_Code[27]), .B26(_32_Bit__Instruction_Code[26]), .RegDst(RegDst),
    .Branch(Branch), .MemRead(MemRead), .MemToReg(MemToReg), .ALUOpHi(ALUOpHi), .ALUOpLow(ALUOpLo),
    .MemWrite(MemWrite), .ALUSrc(ALUSrc), .RegWrite(RegWrite));
  assign bit_extender_1_out = {{16{_32_Bit__Instruction_Code[15]}}, _32_Bit__Instruction_Code[15:0]};  // Bit_Extender bit_extender_1
  Multiplexer #(.width(32), .enable("false")) multiplexer_1 (
    .in0(Register_RT), .in1(bit_extender_1_out), .out(multiplexer_1_out), .sel(ALUSrc));
  Adder #(.width(32)) adder_1 (.a(Register_RS), .b(multiplexer_1_out), .out(adder_1_out));  // open: cin, cout
  Subtractor #(.width(32)) subtractor_1 (
    .a(Register_RS), .b(multiplexer_1_out), .out(subtractor_1_out));  // open: bin, bout
  assign and_1_out = Register_RS & multiplexer_1_out;  // AND_Gate and_1, 32 bits wide
  assign or_1_out = Register_RS | multiplexer_1_out;  // OR_Gate or_1, 32 bits wide
  not not_1 (not_1_out, Register_RS[31]);
  not not_2 (not_2_out, multiplexer_1_out[31]);
  not not_3 (not_3_out, adder_1_out[31]);
  not not_4 (not_4_out, subtractor_1_out[31]);
  _4alu_control_bit_gen ALUControlBits_Generator (
    .ALUOpHi(ALUOpHi), .ALUOpLo(ALUOpLo), .B5(_32_Bit__Instruction_Code[5]),
    .B4(_32_Bit__Instruction_Code[4]), .B3(_32_Bit__Instruction_Code[3]), .B2(_32_Bit__Instruction_Code[2]),
    .B1(_32_Bit__Instruction_Code[1]), .B0(_32_Bit__Instruction_Code[0]), .ALUControl3(out_17),
    .ALUControl2(out_18), .ALUControl1(out_19), .ALUControl0(out_20));
  Multiplexer #(.select(4), .width(32), .enable("false")) multiplexer_2 (
    .in0(and_1_out), .in1(or_1_out), .in2(adder_1_out), .in6(subtractor_1_out), .out(_32_bit_ALU_Output),
    .sel({out_17, out_18, out_19, out_20}));  // open: in3, in4, in5, in7, in8, in9, in10, in11, in12, in13, in14, in15
  and and_2 (and_2_out, not_1_out, not_2_out, adder_1_out[31]);
  and and_3 (and_3_out, Register_RS[31], multiplexer_1_out[31], not_3_out);
  and and_4 (and_4_out, Register_RS[31], not_2_out, not_4_out);
  and and_5 (and_5_out, not_1_out, multiplexer_1_out[31], subtractor_1_out[31]);
  or or_2 (Overflow_Condition, and_2_out, and_5_out);
  buf or_3 (UnderFlow_Condition, and_4_out);  // OR_Gate
  nor nor_1 (Zero, _32_bit_ALU_Output[0], _32_bit_ALU_Output[1], _32_bit_ALU_Output[2], _32_bit_ALU_Output[3], _32_bit_ALU_Output[4], _32_bit_ALU_Output[5], _32_bit_ALU_Output[6], _32_bit_ALU_Output[7], _32_bit_ALU_Output[8], _32_bit_ALU_Output[9], _32_bit_ALU_Output[10], _32_bit_ALU_Output[11], _32_bit_ALU_Output[12], _32_bit_ALU_Output[13], _32_bit_ALU_Output[14], _32_bit_ALU_Output[15], _32_bit_ALU_Output[16], _32_bit_ALU_Output[17], _32_bit_ALU_Output[18], _32_bit_ALU_Output[19], _32_bit_ALU_Output[20], _32_bit_ALU_Output[21], _32_bit_ALU_Output[22], _32_bit_ALU_Output[23], _32_bit_ALU_Output[24], _32_bit_ALU_Output[25], _32_bit_ALU_Output[26], _32_bit_ALU_Output[27], _32_bit_ALU_Output[28], _32_bit_ALU_Output[29], _32_bit_ALU_Output[30], _32_bit_ALU_Output[31]);

  // Notes on the sheet:
  //   OpCode
  //   FunctCode
  //   Computer Architecture 
  //   Lab Assignment 7
endmodule

module control_unit (
  input  B31,
  input  B30,
  input  B29,
  input  B28,
  input  B27,
  input  B26,
  output RegDst,
  output Branch,
  output MemRead,
  output MemToReg,
  output ALUOpHi,
  output ALUOpLow,
  output MemWrite,
  output ALUSrc,
  output RegWrite
);

  wire and_5_out, and_6_out, and_7_out, not_1_out, not_2_out, not_3_out, not_4_out, not_5_out, not_6_out,
       not_7_out, not_8_out, not_9_out, not_10_out;

  not not_1 (not_1_out, B29);
  not not_2 (not_2_out, B27);
  not not_3 (not_3_out, B29);
  not not_4 (not_4_out, B29);
  not not_5 (not_5_out, B28);
  not not_6 (not_6_out, B27);
  and and_1 (MemWrite, B31, B29);
  or or_1 (ALUSrc, B27, B29);
  not not_7 (not_7_out, B28);
  not not_8 (not_8_out, B27);
  not not_9 (not_9_out, B26);
  not not_10 (not_10_out, B29);
  and and_2 (RegDst, not_1_out, not_2_out);
  and and_3 (MemRead, B31, not_3_out);
  and and_4 (ALUOpHi, not_4_out, not_5_out, not_6_out);
  and and_5 (and_5_out, not_7_out, not_8_out);
  and and_6 (and_6_out, B29, not_9_out);
  and and_7 (and_7_out, B31, not_10_out);
  or or_2 (RegWrite, and_5_out, and_6_out, and_7_out);

  assign ALUOpLow = B28;
  assign Branch = B28;
  assign MemToReg = B31;
endmodule

module alu (
);

  wire [3:0] n4alu_control_bit_gen_1_alucontrol0;
  wire [31:0] adder_1_out, and_1_out, or_1_out, subtractor_1_out, undriven, undriven_2;

  Adder #(.width(32)) adder_1 (.a(undriven), .b(undriven_2), .out(adder_1_out));  // open: cin, cout
  Subtractor #(.width(32)) subtractor_1 (.a(undriven), .b(undriven_2), .out(subtractor_1_out));  // open: bin, bout
  assign and_1_out = undriven & undriven_2;  // AND_Gate and_1, 32 bits wide
  assign or_1_out = undriven | undriven_2;  // OR_Gate or_1, 32 bits wide
  _4alu_control_bit_gen u_4alu_control_bit_gen_1 (
    .ALUControl3(n4alu_control_bit_gen_1_alucontrol0[3]),
    .ALUControl2(n4alu_control_bit_gen_1_alucontrol0[2]),
    .ALUControl1(n4alu_control_bit_gen_1_alucontrol0[1]), .ALUControl0(n4alu_control_bit_gen_1_alucontrol0[0]));  // open: ALUOpHi, ALUOpLo, B5, B4, B3, B2, B1, B0
  Multiplexer #(.select(4), .width(32), .enable("false")) multiplexer_1 (
    .in0(and_1_out), .in1(or_1_out), .in2(adder_1_out), .in6(subtractor_1_out),
    .sel(n4alu_control_bit_gen_1_alucontrol0));  // open: in3, in4, in5, in7, in8, in9, in10, in11, in12, in13, in14, in15, out
endmodule

module _4alu_control_bit_gen (
  input  ALUOpHi,
  input  ALUOpLo,
  input  B5,
  input  B4,
  input  B3,
  input  B2,
  input  B1,
  input  B0,
  output ALUControl3,
  output ALUControl2,
  output ALUControl1,
  output ALUControl0
);

  wire and_1_out, and_2_out, and_3_out, not_1_out, not_2_out;

  and and_1 (and_1_out, ALUOpHi, B1);
  not not_1 (not_1_out, ALUOpHi);
  or or_1 (ALUControl1, not_1_out, not_2_out);
  not not_2 (not_2_out, B2);
  and and_2 (and_2_out, ALUOpHi, B0);
  and and_3 (and_3_out, ALUOpHi, B3);
  or or_2 (ALUControl2, ALUOpLo, and_1_out);
  or or_3 (ALUControl0, and_2_out, and_3_out);

  assign ALUControl3 = 1'b0;
endmodule
