// Logisim project B21CS098.circ as structural Verilog: 9 circuits, main circuit Control Unit
module main (
  input  [31:0] Preload_values,
  input  [31:0] Instruction,
  output [1:0] ALU_Opcode,
  output Overflow,
  output Underflow,
  output Zero
);

  wire C, control_unit_1_regwrite;
  wire [3:0] alu_control_1_alu_0;
  wire [31:0] A, B, Write_Data;

  Clock Clock (.out(C));
  Control_Unit control_unit_1 (
    .I31(Instruction[31]), .I30(Instruction[30]), .I29(Instruction[29]), .I28(Instruction[28]),
    .I27(Instruction[27]), .I26(Instruction[26]), .RegWrite(control_unit_1_regwrite), .ALUOp1(ALU_Opcode[1]),
    .ALUOp0(ALU_Opcode[0]));  // open: RegDst, ALUSrc, MemToReg, MemRead, MemWrite, Branch, Jump, ALURequired
  ALU_Control alu_control_1 (
    .ALUOp1(ALU_Opcode[1]), .ALUOp2(ALU_Opcode[0]), .I5(Instruction[5]), .I4(Instruction[4]),
    .I3(Instruction[3]), .I2(Instruction[2]), .I1(Instruction[1]), .I0(Instruction[0]),
    .ALU_3(alu_control_1_alu_0[3]), .ALU_2(alu_control_1_alu_0[2]), .ALU_1(alu_control_1_alu_0[1]),
    .ALU_0(alu_control_1_alu_0[0]));
  RegisterFile registerfile_1 (
    .RegWrite(control_unit_1_regwrite), .rs(Instruction[25:21]), .rt(Instruction[20:16]),
    .rd(Instruction[15:11]), .Write_Data(Write_Data), .in_6(C), .Read_Data_1(A), .Read_Data_2(B));
  // Probe on A
  // Probe on B
  // Probe on Write_Data
  ALU alu_1 (
    .ALU_Control(alu_control_1_alu_0), .A(A), .B(B), .Overflow(Overflow), .Underflow(Underflow), .Zero(Zero),
    .Result(Write_Data));

  // Notes on the sheet:
  //   rs
  //   rt
  //   rd
  //   OpCode
  //   Function Mode
  //   Control Unit
  //   ALU Control
  //   ALU Control output
  //   ALU
endmodule

module Control_Unit (
  input  I31,
  input  I30,
  input  I29,
  input  I28,
  input  I27,
  input  I26,
  output RegDst,
  output ALUSrc,
  output MemToReg,
  output RegWrite,
  output MemRead,
  output MemWrite,
  output Branch,
  output ALUOp1,
  output ALUOp0,
  output Jump,
  output ALURequired
);

  wire and_1_out, and_2_out, and_3_out, and_4_out, not_2_out, not_3_out, not_4_out, not_5_out, not_6_out,
       not_7_out, not_8_out, not_9_out, not_10_out;

  not not_1 (RegDst, I27);
  not not_2 (not_2_out, I28);
  not not_3 (not_3_out, I27);
  not not_4 (not_4_out, I29);
  not not_5 (not_5_out, I27);
  not not_6 (not_6_out, I29);
  not not_7 (not_7_out, I28);
  not not_8 (not_8_out, I27);
  not not_9 (not_9_out, I26);
  not not_10 (not_10_out, I27);
  and and_1 (and_1_out, not_2_out, not_3_out);
  and and_2 (and_2_out, I31, not_4_out);
  and and_3 (and_3_out, I29, not_5_out);
  and and_4 (and_4_out, I31, not_6_out);
  and and_5 (ALUOp1, not_7_out, not_8_out);
  and and_6 (Jump, I27, not_9_out);
  or or_1 (ALURequired, not_10_out, I31);
  or or_2 (RegWrite, and_1_out, and_2_out);
  or or_3 (MemRead, and_3_out, and_4_out);

  assign ALUOp0 = I28;
  assign ALUSrc = I31;
  assign Branch = I28;
  assign MemToReg = I27;
  assign MemWrite = I29;
endmodule

module ALU_Control (
  input  ALUOp1,
  input  ALUOp2,
  input  I5,
  input  I4,
  input  I3,
  input  I2,
  input  I1,
  input  I0,
  output ALU_3,
  output ALU_2,
  output ALU_1,
  output ALU_0
);

  wire and_1_out, and_2_out, and_3_out, not_1_out, not_2_out;

  not not_1 (not_1_out, ALUOp1);
  not not_2 (not_2_out, I2);
  or or_1 (ALU_2, ALUOp2, and_1_out);
  and and_1 (and_1_out, ALUOp1, I1);
  or or_2 (ALU_1, not_1_out, not_2_out);
  and and_2 (and_2_out, ALUOp1, I0);
  or or_3 (ALU_0, and_2_out, and_3_out);
  and and_3 (and_3_out, ALUOp1, I3);

  assign ALU_3 = 1'b0;
endmodule

module ALU (
  input  [3:0] ALU_Control,
  input  [31:0] A,
  input  [31:0] B,
  output Overflow,
  output Underflow,
  output Zero,
  output [31:0] Result
);

  wire comparator_1_lt, Overflow_t, Underflow_t;
  wire [31:0] adder_1_out_3, and_1_out, bit_extender_1_out, or_1_out, subtractor_1_out_3;

  assign and_1_out = A & B;  // AND_Gate and_1, 32 bits wide
  assign or_1_out = A | B;  // OR_Gate or_1, 32 bits wide
  Adder adder_1 (.in_1(A), .in_2(B), .out_3(adder_1_out_3), .out_4(Overflow_t));
  Subtractor subtractor_1 (.in_1(A), .in_2(B), .out_3(subtractor_1_out_3), .out_4(Underflow_t));
  Comparator #(.width(32)) comparator_1 (.a(A), .b(B), .lt(comparator_1_lt));  // open: gt, eq
  assign bit_extender_1_out = {{31{1'b0}}, comparator_1_lt};  // Bit_Extender bit_extender_1
  Multiplexer #(.select(4), .width(32), .enable("false")) multiplexer_1 (
    .in0(and_1_out), .in1(or_1_out), .in2(adder_1_out_3), .in6(subtractor_1_out_3), .in7(bit_extender_1_out),
    .out(Result), .sel(ALU_Control));  // open: in3, in4, in5, in8, in9, in10, in11, in12, in13, in14, in15
  Zero_Detection_Unit zero_detection_unit_1 (.in_1(Result), .out_2(Zero));
  and and_2 (Overflow, ~ALU_Control[3], ~ALU_Control[2], ALU_Control[1], ~ALU_Control[0], Overflow_t);  // AND_Gate
  and and_3 (Underflow, ~ALU_Control[3], ALU_Control[2], ALU_Control[1], ~ALU_Control[0], Underflow_t);  // AND_Gate

  // Notes on the sheet:
  //   AND
  //   OR
  //   ADD
  //   SUB
  //   SLT
  //   Adder
  //   Subtractor
  //   zero
  //   unit
endmodule

module Zero_Detection_Unit (
  input  [31:0] in_1,
  output out_2
);

  wire or_1_out;

  not not_1 (out_2, or_1_out);
  or or_1 (or_1_out, in_1[0], in_1[1], in_1[2], in_1[3], in_1[4], in_1[5], in_1[6], in_1[7], in_1[8], in_1[9], in_1[10], in_1[11], in_1[12], in_1[13], in_1[14], in_1[15], in_1[17], in_1[18], in_1[19], in_1[20], in_1[21], in_1[22], in_1[23], in_1[24], in_1[25], in_1[26], in_1[27], in_1[28], in_1[29], in_1[30], in_1[31], in_1[16]);

  // Other names for the same wires on the sheet: _15 = in_1[16]

  // Notes on the sheet:
  //   ZERO DETECTION UNIT
endmodule

module Adder (
  input  [31:0] in_1,
  input  [31:0] in_2,
  output [31:0] out_3,
  output out_4
);

  wire adder_1_cout, adder_2_cout;

  Adder_part #(.width(31)) adder_1 (.a(in_1[30:0]), .b(in_2[30:0]), .out(out_3[30:0]), .cin(1'b0), .cout(adder_1_cout));
  Adder_part #(.width(1)) adder_2 (
    .a(in_1[31]), .b(in_2[31]), .out(out_3[31]), .cin(adder_1_cout), .cout(adder_2_cout));
  xor xor_1 (out_4, adder_1_cout, adder_2_cout);
endmodule

module Subtractor (
  input  [31:0] in_1,
  input  [31:0] in_2,
  output [31:0] out_3,
  output out_4
);

  wire adder_1_cout, adder_2_cout;
  wire [31:0] not_1_out;

  assign not_1_out = ~in_2;  // NOT_Gate not_1, 32 bits wide
  Adder_part #(.width(31)) adder_1 (
    .a(in_1[30:0]), .b(not_1_out[30:0]), .out(out_3[30:0]), .cin(1'b1), .cout(adder_1_cout));
  Adder_part #(.width(1)) adder_2 (
    .a(in_1[31]), .b(not_1_out[31]), .out(out_3[31]), .cin(adder_1_cout), .cout(adder_2_cout));
  xor xor_1 (out_4, adder_1_cout, adder_2_cout);
endmodule

module RegisterFile (
  input  RegWrite,
  input  [4:0] rs,
  input  [4:0] rt,
  input  [4:0] rd,
  input  [31:0] Write_Data,
  input  in_6,
  output [31:0] Read_Data_1,
  output [31:0] Read_Data_2
);

  wire [31:0] Registers__0, Registers__1, Registers__2, Registers__3, Registers_out_9, Registers_out_10,
       Registers_out_11, Registers_out_12, Registers_out_13, Registers_out_14, Registers_out_15,
       Registers_out_16, Registers_out_17, Registers_out_18, Registers_out_19, Registers_out_20,
       Registers_out_21, Registers_out_22, Registers_out_23, Registers_out_24, Registers_out_25,
       Registers_out_26, Registers_out_27, Registers_out_28, Registers_out_29, Registers_out_30,
       Registers_out_31, Registers_out_32, Registers_out_33, Registers_out_34, Registers_out_35,
       Registers_out_36;

  Registers Registers (
    .Clock(in_6), .RegWrite(RegWrite), .Write_Data(Write_Data), .rd(rd), ._0(Registers__0),
    ._1(Registers__1), ._2(Registers__2), ._3(Registers__3), .out_9(Registers_out_9),
    .out_10(Registers_out_10), .out_11(Registers_out_11), .out_12(Registers_out_12),
    .out_13(Registers_out_13), .out_14(Registers_out_14), .out_15(Registers_out_15),
    .out_16(Registers_out_16), .out_17(Registers_out_17), .out_18(Registers_out_18),
    .out_19(Registers_out_19), .out_20(Registers_out_20), .out_21(Registers_out_21),
    .out_22(Registers_out_22), .out_23(Registers_out_23), .out_24(Registers_out_24),
    .out_25(Registers_out_25), .out_26(Registers_out_26), .out_27(Registers_out_27),
    .out_28(Registers_out_28), .out_29(Registers_out_29), .out_30(Registers_out_30),
    .out_31(Registers_out_31), .out_32(Registers_out_32), .out_33(Registers_out_33),
    .out_34(Registers_out_34), .out_35(Registers_out_35), .out_36(Registers_out_36));
  Multiplexer #(.select(5), .width(32), .enable("false")) multiplexer_1 (
    .in0(Registers__0), .in1(Registers__1), .in2(Registers__2), .in3(Registers__3), .in4(Registers_out_9),
    .in5(Registers_out_10), .in6(Registers_out_11), .in7(Registers_out_12), .in8(Registers_out_13),
    .in9(Registers_out_14), .in10(Registers_out_15), .in11(Registers_out_16), .in12(Registers_out_17),
    .in13(Registers_out_18), .in14(Registers_out_19), .in15(Registers_out_20), .in16(Registers_out_21),
    .in17(Registers_out_22), .in18(Registers_out_23), .in19(Registers_out_24), .in20(Registers_out_25),
    .in21(Registers_out_26), .in22(Registers_out_27), .in23(Registers_out_28), .in24(Registers_out_29),
    .in25(Registers_out_30), .in26(Registers_out_31), .in27(Registers_out_32), .in28(Registers_out_33),
    .in29(Registers_out_34), .in30(Registers_out_35), .in31(Registers_out_36), .out(Read_Data_1), .sel(rs));
  Multiplexer #(.select(5), .width(32), .enable("false")) multiplexer_2 (
    .in0(Registers__0), .in1(Registers__1), .in2(Registers__2), .in3(Registers__3), .in4(Registers_out_9),
    .in5(Registers_out_10), .in6(Registers_out_11), .in7(Registers_out_12), .in8(Registers_out_13),
    .in9(Registers_out_14), .in10(Registers_out_15), .in11(Registers_out_16), .in12(Registers_out_17),
    .in13(Registers_out_18), .in14(Registers_out_19), .in15(Registers_out_20), .in16(Registers_out_21),
    .in17(Registers_out_22), .in18(Registers_out_23), .in19(Registers_out_24), .in20(Registers_out_25),
    .in21(Registers_out_26), .in22(Registers_out_27), .in23(Registers_out_28), .in24(Registers_out_29),
    .in25(Registers_out_30), .in26(Registers_out_31), .in27(Registers_out_32), .in28(Registers_out_33),
    .in29(Registers_out_34), .in30(Registers_out_35), .in31(Registers_out_36), .out(Read_Data_2), .sel(rt));

  // Other names for the same wires on the sheet: Clock = in_6
endmodule

module Registers (
  input  Clock,
  input  RegWrite,
  input  [31:0] Write_Data,
  input  [4:0] rd,
  output [31:0] _0,
  output [31:0] _1,
  output [31:0] _2,
  output [31:0] _3,
  output [31:0] out_9,
  output [31:0] out_10,
  output [31:0] out_11,
  output [31:0] out_12,
  output [31:0] out_13,
  output [31:0] out_14,
  output [31:0] out_15,
  output [31:0] out_16,
  output [31:0] out_17,
  output [31:0] out_18,
  output [31:0] out_19,
  output [31:0] out_20,
  output [31:0] out_21,
  output [31:0] out_22,
  output [31:0] out_23,
  output [31:0] out_24,
  output [31:0] out_25,
  output [31:0] out_26,
  output [31:0] out_27,
  output [31:0] out_28,
  output [31:0] out_29,
  output [31:0] out_30,
  output [31:0] out_31,
  output [31:0] out_32,
  output [31:0] out_33,
  output [31:0] out_34,
  output [31:0] out_35,
  output [31:0] out_36
);

  wire a0_out, a1_out, a2_out, a3_out, at_out, decoder_1_out0, decoder_1_out1, decoder_1_out2,
       decoder_1_out3, decoder_1_out4, decoder_1_out5, decoder_1_out6, decoder_1_out7, decoder_1_out8,
       decoder_1_out9, decoder_1_out10, decoder_1_out11, decoder_1_out12, decoder_1_out13, decoder_1_out14,
       decoder_1_out15, decoder_1_out16, decoder_1_out17, decoder_1_out18, decoder_1_out19, decoder_1_out20,
       decoder_1_out21, decoder_1_out22, decoder_1_out23, decoder_1_out24, decoder_1_out25, decoder_1_out26,
       decoder_1_out27, decoder_1_out28, decoder_1_out29, decoder_1_out30, decoder_1_out31, fp_out, gp_out,
       k0_out, k1_out, ra_out, s0_out, s1_out, s2_out, s3_out, s4_out, s5_out, s6_out, s7_out, sp_out,
       t0_out, t1_out, t2_out, t3_out, t4_out, t5_out, t6_out, t7_out, t8_out, t9_out, v0_out, v1_out,
       zero_out;

  Decoder #(.select(5)) decoder_1 (
    .out0(decoder_1_out0), .out1(decoder_1_out1), .out2(decoder_1_out2), .out3(decoder_1_out3),
    .out4(decoder_1_out4), .out5(decoder_1_out5), .out6(decoder_1_out6), .out7(decoder_1_out7),
    .out8(decoder_1_out8), .out9(decoder_1_out9), .out10(decoder_1_out10), .out11(decoder_1_out11),
    .out12(decoder_1_out12), .out13(decoder_1_out13), .out14(decoder_1_out14), .out15(decoder_1_out15),
    .out16(decoder_1_out16), .out17(decoder_1_out17), .out18(decoder_1_out18), .out19(decoder_1_out19),
    .out20(decoder_1_out20), .out21(decoder_1_out21), .out22(decoder_1_out22), .out23(decoder_1_out23),
    .out24(decoder_1_out24), .out25(decoder_1_out25), .out26(decoder_1_out26), .out27(decoder_1_out27),
    .out28(decoder_1_out28), .out29(decoder_1_out29), .out30(decoder_1_out30), .out31(decoder_1_out31),
    .sel(rd), .en(RegWrite));
  buf zero (zero_out, decoder_1_out0);  // AND_Gate
  and at (at_out, RegWrite, decoder_1_out1);
  and v0 (v0_out, RegWrite, decoder_1_out2);
  and v1 (v1_out, RegWrite, decoder_1_out3);
  and a0 (a0_out, decoder_1_out4, RegWrite);
  and a1 (a1_out, decoder_1_out5, RegWrite);
  and a2 (a2_out, decoder_1_out6, RegWrite);
  and a3 (a3_out, decoder_1_out7, RegWrite);
  Register #(.width(32)) register_1 (.D(Write_Data), .en(zero_out), .Q(_0), .clk(Clock));  // open: clr
  Register #(.width(32)) register_2 (.D(Write_Data), .en(at_out), .Q(_1), .clk(Clock));  // open: clr
  Register #(.width(32)) register_3 (.D(Write_Data), .en(v0_out), .Q(_2), .clk(Clock));  // open: clr
  Register #(.width(32)) register_4 (.D(Write_Data), .en(v1_out), .Q(_3), .clk(Clock));  // open: clr
  Register #(.width(32)) register_5 (.D(Write_Data), .en(a0_out), .Q(out_9), .clk(Clock));  // open: clr
  Register #(.width(32)) register_6 (.D(Write_Data), .en(a1_out), .Q(out_10), .clk(Clock));  // open: clr
  Register #(.width(32)) register_7 (.D(Write_Data), .en(a2_out), .Q(out_11), .clk(Clock));  // open: clr
  Register #(.width(32)) register_8 (.D(Write_Data), .en(a3_out), .Q(out_12), .clk(Clock));  // open: clr
  Register #(.width(32)) register_9 (.D(Write_Data), .en(t0_out), .Q(out_13), .clk(Clock));  // open: clr
  and t0 (t0_out, RegWrite, decoder_1_out8);
  Register #(.width(32)) register_10 (.D(Write_Data), .en(t1_out), .Q(out_14), .clk(Clock));  // open: clr
  and t1 (t1_out, RegWrite, decoder_1_out9);
  Register #(.width(32)) register_11 (.D(Write_Data), .en(t2_out), .Q(out_15), .clk(Clock));  // open: clr
  and t2 (t2_out, RegWrite, decoder_1_out10);
  Register #(.width(32)) register_12 (.D(Write_Data), .en(t3_out), .Q(out_16), .clk(Clock));  // open: clr
  and t3 (t3_out, RegWrite, decoder_1_out11);
  Register #(.width(32)) register_13 (.D(Write_Data), .en(t4_out), .Q(out_17), .clk(Clock));  // open: clr
  and t4 (t4_out, decoder_1_out12, RegWrite);
  Register #(.width(32)) register_14 (.D(Write_Data), .en(t5_out), .Q(out_18), .clk(Clock));  // open: clr
  and t5 (t5_out, decoder_1_out13, RegWrite);
  Register #(.width(32)) register_15 (.D(Write_Data), .en(t6_out), .Q(out_19), .clk(Clock));  // open: clr
  and t6 (t6_out, decoder_1_out14, RegWrite);
  Register #(.width(32)) register_16 (.D(Write_Data), .en(t7_out), .Q(out_20), .clk(Clock));  // open: clr
  and t7 (t7_out, decoder_1_out15, RegWrite);
  Register #(.width(32)) register_17 (.D(Write_Data), .en(s0_out), .Q(out_21), .clk(Clock));  // open: clr
  and s0 (s0_out, RegWrite, decoder_1_out16);
  Register #(.width(32)) register_18 (.D(Write_Data), .en(s1_out), .Q(out_22), .clk(Clock));  // open: clr
  and s1 (s1_out, RegWrite, decoder_1_out17);
  Register #(.width(32)) register_19 (.D(Write_Data), .en(s2_out), .Q(out_23), .clk(Clock));  // open: clr
  and s2 (s2_out, RegWrite, decoder_1_out18);
  Register #(.width(32)) register_20 (.D(Write_Data), .en(s3_out), .Q(out_24), .clk(Clock));  // open: clr
  and s3 (s3_out, RegWrite, decoder_1_out19);
  Register #(.width(32)) register_21 (.D(Write_Data), .en(s4_out), .Q(out_25), .clk(Clock));  // open: clr
  and s4 (s4_out, decoder_1_out20, RegWrite);
  Register #(.width(32)) register_22 (.D(Write_Data), .en(s5_out), .Q(out_26), .clk(Clock));  // open: clr
  and s5 (s5_out, decoder_1_out21, RegWrite);
  Register #(.width(32)) register_23 (.D(Write_Data), .en(s6_out), .Q(out_27), .clk(Clock));  // open: clr
  and s6 (s6_out, decoder_1_out22, RegWrite);
  Register #(.width(32)) register_24 (.D(Write_Data), .en(s7_out), .Q(out_28), .clk(Clock));  // open: clr
  and s7 (s7_out, decoder_1_out23, RegWrite);
  and t8 (t8_out, RegWrite, decoder_1_out24);
  and t9 (t9_out, RegWrite, decoder_1_out25);
  and k0 (k0_out, RegWrite, decoder_1_out26);
  and k1 (k1_out, RegWrite, decoder_1_out27);
  and gp (gp_out, decoder_1_out28, RegWrite);
  and sp (sp_out, decoder_1_out29, RegWrite);
  and fp (fp_out, decoder_1_out30, RegWrite);
  and ra (ra_out, decoder_1_out31, RegWrite);
  Register #(.width(32)) register_25 (.D(Write_Data), .en(t8_out), .Q(out_29), .clk(Clock));  // open: clr
  Register #(.width(32)) register_26 (.D(Write_Data), .en(t9_out), .Q(out_30), .clk(Clock));  // open: clr
  Register #(.width(32)) register_27 (.D(Write_Data), .en(k0_out), .Q(out_31), .clk(Clock));  // open: clr
  Register #(.width(32)) register_28 (.D(Write_Data), .en(k1_out), .Q(out_32), .clk(Clock));  // open: clr
  Register #(.width(32)) register_29 (.D(Write_Data), .en(gp_out), .Q(out_33), .clk(Clock));  // open: clr
  Register #(.width(32)) register_30 (.D(Write_Data), .en(sp_out), .Q(out_34), .clk(Clock));  // open: clr
  Register #(.width(32)) register_31 (.D(Write_Data), .en(fp_out), .Q(out_35), .clk(Clock));  // open: clr
  Register #(.width(32)) register_32 (.D(Write_Data), .en(ra_out), .Q(out_36), .clk(Clock));  // open: clr

  // Other names for the same wires on the sheet: _4[31:0] = out_9; _5[31:0] = out_10; _6[31:0] = out_11;
  //   _7[31:0] = out_12; _8[31:0] = out_13; _9[31:0] = out_14; _10[31:0] = out_15; _11[31:0] = out_16;
  //   _12[31:0] = out_17; _13[31:0] = out_18; _14[31:0] = out_19; _15[31:0] = out_20; _16[31:0] = out_21;
  //   _17[31:0] = out_22; _18[31:0] = out_23; _19[31:0] = out_24; _20[31:0] = out_25; _21[31:0] = out_26;
  //   _22[31:0] = out_27; _23[31:0] = out_28; _24[31:0] = out_29; _25[31:0] = out_30; _26[31:0] = out_31;
  //   _27[31:0] = out_32; _28[31:0] = out_33; _29[31:0] = out_34; _30[31:0] = out_35; _31[31:0] = out_36

  // Notes on the sheet:
  //   Outputs are taken in this form to ease out the multiplexer inputs in the RegisterFile subcircuit
endmodule
